// Logisim project cir_00_template.circ as structural Verilog: 1 circuit, main circuit main
module main (
  input  A,
  input  B,
  input  C,
  output notA,
  output notB,
  output notC
);

  not not_1 (notA, A);
  not not_2 (notB, B);
  not not_3 (notC, C);
endmodule
