// Logisim project cir_01_multiplexer.circ as structural Verilog: 1 circuit, main circuit main
module main (
  input  A,
  input  B,
  input  C,
  output notA,
  output notB,
  output notC,
  output out_7
);

  wire and_1_out, and_2_out;

  not not_1 (notA, A);
  not not_2 (notB, B);
  not not_3 (notC, C);
  and and_1 (and_1_out, A, notC);
  and and_2 (and_2_out, B, C);
  or or_1 (out_7, and_1_out, and_2_out);
endmodule
