// Logisim project cir_02_digital_tranformer8.circ as structural Verilog: 1 circuit, main circuit main
module main (
  input  a3,
  input  a2,
  input  a1,
  input  a0
);

  wire and_1_out, and_2_out, not_1_out, not_2_out, not_3_out, not_4_out, or_1_out, or_2_out, or_3_out,
       or_4_out, or_5_out, or_6_out, or_7_out, or_8_out, or_9_out;

  not not_1 (not_1_out, a3);
  not not_2 (not_2_out, a2);
  not not_3 (not_3_out, a1);
  not not_4 (not_4_out, a0);
  or or_1 (or_1_out, a1, not_2_out);
  or or_2 (or_2_out, not_3_out, a0);
  or or_3 (or_3_out, not_1_out, a0);
  or or_4 (or_4_out, a3, not_3_out);
  or or_5 (or_5_out, not_2_out, not_4_out);
  or or_6 (or_6_out, not_1_out, not_3_out, not_4_out);
  or or_7 (or_7_out, not_1_out, a1, a0);
  or or_8 (or_8_out, not_1_out, not_2_out);
  or or_9 (or_9_out, not_2_out, not_3_out);
  LED module_A (.in(and_1_out));
  and and_1 (and_1_out, or_1_out, or_2_out, or_3_out, or_4_out, or_5_out);
  LED module_A_2 (.in(and_2_out));
  and and_2 (and_2_out, or_6_out, or_7_out, or_8_out, or_9_out);

  // Notes on the sheet:
  //   na2
  //   na3
  //   na0
  //   na1
endmodule
